# Fritzing sketch Mon_montage_hydro_system_final (saved by Fritzing 0.9.3b)
breadboards: 2

parts:
  ESP32 = ESP32 DevKitc V4
  JACK1 = 2.1mm Barrel Jack with Terminal Block
  LED1 = smd LED [color="Red (633nm)" package="0603 [SMD]"]
  R1 = Resistor [tolerance=±5% resistance=220 package="1206 [SMD]"]
  LED2 = smd LED [color="Red (633nm)" package="0603 [SMD]"]
  R2 = Resistor [tolerance=±5% resistance=220 package="1206 [SMD]"]
  LED3 = smd LED [color="Red (633nm)" package="0603 [SMD]"]
  R3 = Resistor [tolerance=±5% resistance=220 package="1206 [SMD]"]
  LED4 = smd LED [color="Red (633nm)" package="0603 [SMD]"]
  R4 = Resistor [tolerance=±5% resistance=220 package="1206 [SMD]"]
  Servo1 = Basic Servo
  Water_pump = DC Motor
  KY-1 = Keyes Relay [package=THT]
  TDS = tds-sensor-meter-v1.0_1
  pH = PH meter [package=THT]
  R5 = Resistor [tolerance=±5% resistance=10k package="1206 [SMD]"]
  R6 = Resistor [tolerance=±5% resistance=20k package="1206 [SMD]"]
  R7 = PHOTOCELL [package=photocell]
  KY-2 = Keyes Relay [package=THT]
  Fan = Fan - Ventilador [package=THT]
  Water_level = water level switch
  DHT22 = Humidity and Temperature Sensor RHT03
  R9 = Resistor [tolerance=±5% resistance=10k package="1206 [SMD]"]
  Servo2 = Basic Servo
  LED5 = smd LED [color="Red (633nm)" package="0603 [SMD]"]
  R10 = Resistor [tolerance=±5% resistance=220 package="1206 [SMD]"]
  R8 = Resistor [tolerance=±5% resistance=10k package="1206 [SMD]"]
  R11 = Resistor [tolerance=±5% resistance=20k package="1206 [SMD]"]  # not connected

nets:
  N1: ESP32.IO18, KY-2.signal
  N2: ESP32.IO19, Water_level.pin2
  N3: ESP32.IO21, DHT22.Data-signal, R9.Pin_1
  N4: ESP32.IO22, Servo2.pulse
  N5: ESP32.IO23, R10.Pin_1
  3V3: ESP32.3V3, DHT22.Vcc, R9.Pin_0
  N6: ESP32.VP, R7.P$2, R8.Pin_0
  N7: ESP32.VN, R5.Pin_0, R6.Pin_0
  N8: ESP32.IO34, TDS.pin1
  N9: ESP32.IO32, KY-1.signal
  N10: ESP32.IO33, Servo1.pulse
  N11: ESP32.IO25, R4.Pin_1
  N12: ESP32.IO26, R3.Pin_1
  N13: ESP32.IO27, R2.Pin_1
  N14: ESP32.IO14, R1.Pin_1
  GND: ESP32.GND, LED1.cathode, LED2.cathode, LED3.cathode, LED4.cathode, Servo1.gnd, KY-1.ground, TDS.pin3, pH.pin3, R6.Pin_1, KY-2.ground, Water_level.pin1, DHT22.GND_2, Servo2.gnd, LED5.cathode, R8.Pin_1
  VCC: ESP32.5V, Servo1.vcc, KY-1.power, TDS.pin2, pH.pin2, R7.P$1, KY-2.power, Servo2.vcc
  N15: JACK1.POS, KY-1.NO, KY-2.NO
  N16: JACK1.NEG, Fan.GND
  N17: LED1.anode, R1.Pin_0
  N18: LED2.anode, R2.Pin_0
  N19: LED3.anode, R3.Pin_0
  N20: LED4.anode, R4.Pin_0
  N21: Water_pump.pin_2, KY-1.C
  N22: pH.pin1, R5.Pin_1
  N23: KY-2.C, Fan.5V
  N24: LED5.anode, R10.Pin_0

custom parts:
  ESP32 DevKitc V4: ESP32-DevKitC board with ESP32-WROOM-32 module. ESP32-DevKitC V4 is a small-sized ESP32-based development board produced by Espressif. Most of the pins on the ESP module are broken out to the pin headers on the board. The pins D0, D1, D2, D3, CMD and CLK are used internally for communication between ESP32 and SPI flash memory. They are grouped on both sides near the USB connector. Avoid using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
  Keyes Relay: The Keyes 5V relay module is suitable for SCM development, home appliance control. It uses a 5V~12V TIL control signal which can control DC / AC signal.
  : TDS Meter V1.0 Development Board Water Meter Filter Measuring Water Sensor Module.
  Fan - Ventilador: Ventilador de 2 pines, se encuentra comunmente en computadoras de escritorio
  water level switch: Generic water level float switch.
